# Fritzing sketch WindFoxUno (saved by Fritzing 0.9.3b)
breadboards: 1

parts:
  U1 = Sharp Dust Sensor [part_number=GP2Y1010AU0F]
  RHT1 = Humidity and Temperature Sensor RHT03
  R2 = Resistor [tolerance=±5% resistance=150 package=THT]
  C1 = Electrolytic Capacitor [capacitance=1µF package="100 mil [THT, electrolytic]"]
  부품1 = Arduino Uno (Rev3)
  WaveShare_1_3inch_OLED_128x64_I2C = WaveShare 1.3inch OLED 128x64
  부품2 = NeoPixel Stick [part_number=1426]
  SLEEP = Pushbutton [package="[THT]"]
  MAX_SPEED = Pushbutton [package="[THT]"]
  J1 = female pin header, 2 pins [form="♀ (female)"]
  J2 = female pin header, 2 pins [form="♀ (female)"]
  J3 = female pin header, 2 pins [form="♀ (female)"]
  J4 = female pin header, 2 pins [form="♀ (female)"]

nets:
  N1: U1.V-LED, R2.Pin_1, C1.+
  GND: U1.LED-GND, U1.S-GND, RHT1.GND_1, RHT1.GND_2, C1.-, 부품1.GND, WaveShare_1_3inch_OLED_128x64_I2C.GND, 부품2.GND
  N2: U1.LED, 부품1.D7
  N3: U1.Vo, 부품1.A0
  +12V_FAN/5V: U1.VCC, RHT1.Vcc, R2.Pin_0, 부품1.VIN, WaveShare_1_3inch_OLED_128x64_I2C.VCC, 부품2.+5V, SLEEP.Pin_1, SLEEP.Pin_2, MAX_SPEED.Pin_3, MAX_SPEED.Pin_4
  N4: RHT1.Data-signal, 부품1.D12/MISO
  N5: 부품1.A3, MAX_SPEED.Pin_1
  N6: 부품1.A4/SDA, WaveShare_1_3inch_OLED_128x64_I2C.DIN
  N7: 부품1.A5/SCL, WaveShare_1_3inch_OLED_128x64_I2C.CLK
  N8: 부품1.D8, 부품2.DATAIN
  FAN_PWM2: 부품1.D9_PWM, J2.pin1
  FAN_PWM3: 부품1.D10_PWM/SS, J3.pin1
  FAN_PWM4: 부품1.D11_PWM/MOSI, J4.pin1
  FAN_SPEED1: 부품1.D13/SCK, J1.pin2
  N9: 부품1.D2, SLEEP.Pin_3, SLEEP.Pin_4
  FAN_SPEED2: 부품1.D3_PWM, J2.pin2
  FAN_SPEED3: 부품1.D4, J3.pin2
  FAN_SPEED4: 부품1.D5_PWM, J4.pin2
  FAN_PWM1: 부품1.D6_PWM, J1.pin1

custom parts:
  Sharp Dust Sensor: Sharp GP2Y1010AU0F Dust Sensor
  WaveShare 1.3inch OLED 128x64: OLED
  NeoPixel Stick: Make your own little LED strip arrangement with this stick of NeoPixel LEDs. We crammed 8 of the tiny 5050 (5mm x 5mm) smart RGB LEDs onto a PCB with mounting holes and a chainable design. Use only one microcontroller pin to control as many as you can chain together! Each LED is addressable as the driver chip is inside the LED. Each one has ~18mA constant current drive so the color will be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
